// Logisim project Lab3.circ as structural Verilog: 1 circuit, main circuit main
// Odd Parity
module main (
  input  [3:0] in_1,
  input  [3:0] in_2,
  input  [3:0] in_3,
  input  [3:0] in_4,
  input  in_5,
  input  in_6,
  input  in_7,
  input  in_8,
  input  in_9,
  input  in_10,
  input  in_11,
  input  in_12,
  input  in_13,
  input  in_14,
  input  in_15,
  input  in_16,
  output [4:0] out_17,
  output [3:0] out_18,
  output out_19,
  output out_20
);

  wire adder_1_cout;
  wire [3:0] adder_1_out;

  Adder #(.width(4)) adder_1 (.a(in_1), .b(in_2), .out(adder_1_out), .cout(adder_1_cout));  // open: cin
  Subtractor #(.width(4)) subtractor_1 (.a(in_3), .b(in_4), .out(out_18));  // open: bin, bout
  xor Odd_Parity (out_19, in_5, in_6, in_7, in_8, in_9, in_10);
  xnor Even_Parity (out_20, in_11, in_12, in_13, in_14, in_15, in_16);
  assign out_17 = {{1{adder_1_cout}}, adder_1_out};  // Bit_Extender bit_extender_1

  // Notes on the sheet:
  //   Adder
  //   Subtractor
endmodule
